# Fritzing sketch alarm (saved by Fritzing 0.9.3b)
breadboards: 1

parts:
  Part1 = Arduino Uno (Rev3) - ICSP
  R1 = Resistor [tolerance=±5% resistance=220 package=THT]
  LED1 = LED - 5mm [color="Red (633nm)" package="5 mm [THT]"]
  J1 = Piezo Speaker
  S1 = Pushbutton [package="[THT]"]
  Part2 = Thumb Joystick

nets:
  N1: Part1.D8, J1.pin2
  N2: Part1.D9_PWM, LED1.cathode
  GND: Part1.GND, S1.Pin_1, S1.Pin_2, Part2.GND
  N3: Part1.D3_PWM, S1.Pin_3, S1.Pin_4
  N4: Part1.D5_PWM, Part2.SEL
  N5: Part1.5V, R1.Pin_1, J1.pin1, Part2.HORZ
  N6: R1.Pin_0, LED1.anode
